# Fritzing sketch AutomationsESP32 (saved by Fritzing 0.9.3b)
breadboards: 1

parts:
  U2 = ESP8266 NodeMCU LoLin base
  DHT1 = Humidity and Temperature Sensor DHT11
  LCD2004-I2C1 = LCD2004-I2C
  U3 = 16-Channel Relay Module [package=relay-16ch]
  Part1 = Black Joystick KY-023
  LED1 = LEDs [package=led10mm]
  Power_plug1 = Power plug

nets:
  GND: U2.GND1-0, U2.GND1-2, U2.GND1-3, U2.GND8-0, U2.GND8-4, U2.GND8-10, DHT1.GND_2, LCD2004-I2C1.GND, U3.OUT_GND, Part1.GND
  VCC: U2.3V1-0, U2.3V1-1, U2.3V1-2, U2.3V1-3, DHT1.Vcc, U3.VCCOUT_5V, Part1.+5V
  N1: U2.D1-3, LCD2004-I2C1.SCL
  N2: U2.D2-3, LCD2004-I2C1.SDA
  N3: U2.D4-3, U3.IN1
  N4: U2.D5-0, U2.D5-1, U2.D5-3, DHT1.Data-signal
  N5: U2.VUSB-0, LCD2004-I2C1.VCC, U3.K14_COM
  N6: U3.K1_NO, LED1.A
  N7: U3.K1_COM, Power_plug1.VCC
  N8: LED1.C, Power_plug1.GND

custom parts:
  ESP8266 NodeMCU LoLin base: ESP8266 based NodeMCU Base
  Humidity and Temperature Sensor DHT11: Digital relative humidity & temperature sensor DHT11
  LCD2004-I2C: A standard character display with 4x20 characters. Comes in many colors with LCM2004 IIC attached.
  16-Channel Relay Module: 16 channel relay module
  Black Joystick KY-023: Description: The joystick is a combination of 2 analoog potentiometer and a digital switch. Arduino GND --> Module pin - Arduino +5V --> Module pin +5V Arduino Analoog 0 --> Module VRx Arduino Analoog 1 --> Module VRy Arduino Digital --> Module SW Dimensions: 1" x 1.25"
  LEDs: LEDs Standard schematic elements and footprints for 5mm, 3mm, 1206, and 0603 sized LEDs. 5mm - Spark Fun Electronics SKU : COM-00529 (and others)
